# Fritzing sketch schematics (saved by Fritzing 0.9.3b)
breadboards: 1

parts:
  Arduino_Pro_Mini_3_3V = Arduino Pro Mini (3.3V)
  L298N_driver_board = L298N DC motor driver
  12V_DC_motor = DC Motor
  Photocell = KY-018 Photoresistor Module [package="Breakout board"]
  VCC1 = 4 x AAA Battery Mount
  VCC2 = 4 x AAA Battery Mount
  VCC3 = 4 x AAA Battery Mount
  VCC4 = 4 x AAA Battery Mount
  Top_Switch = SPST Slide Switch [package="SIP THT"]
  Bottom_Switch = SPST Slide Switch [package="SIP THT"]
  12V_2_8Ah_battery = 12 battery [package=battery]

nets:
  GND: Arduino_Pro_Mini_3_3V.GND, Photocell.Vin, Top_Switch.L2, Bottom_Switch.L2
  N1: Arduino_Pro_Mini_3_3V.A3, Photocell.S
  N2: Arduino_Pro_Mini_3_3V.SCK, Photocell.-
  N3: Arduino_Pro_Mini_3_3V.MOSI, L298N_driver_board.5V#7
  N4: Arduino_Pro_Mini_3_3V.D8, L298N_driver_board.IN2
  N5: Arduino_Pro_Mini_3_3V.D7, L298N_driver_board.5V#9, L298N_driver_board.ENA, L298N_driver_board.IN1
  N6: Arduino_Pro_Mini_3_3V.D3, Bottom_Switch.L1, Bottom_Switch.COM
  N7: Arduino_Pro_Mini_3_3V.D2, Top_Switch.L1
  N8: L298N_driver_board.OUT1, 12V_DC_motor.pin_2
  N9: L298N_driver_board.OUT2, 12V_DC_motor.pin_1
  N10: L298N_driver_board.12V, 12V_2_8Ah_battery.+
  N11: L298N_driver_board.GND, 12V_2_8Ah_battery.-
  N12: VCC1.-, VCC4.+
  N13: VCC1.+, VCC3.+
  N14: VCC2.-, VCC4.-
  N15: VCC2.+, VCC3.-

custom parts:
  L298N DC motor driver: 2x DC motor driver with 78M05 positive voltage regulator (7..35 V) L298N: max 46 V, 2 A Set 5 V Enable jumper to enable 5 V regultor (needed for the L298N) and +5 V output at screw terminal or supply external +5 V at screw terminal Set ENA and/or ENB to +5 V to enable motor permanently or supply ENA and/or ENB with PWM signal IN1 and IN2 set rotation directory for motor A (OUT1/OUT2) IN2 and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
  KY-018 Photoresistor Module: KY-018 Photoresistor module, used to measure light intensity. It can determine the presence or absence of light.
  SPST Slide Switch: SPST slide switch with inline 100mil spacing through hole connection terminals
  12 battery: 12V lead acid type battery, like the Husqvarna YTH2448 12V 35AH battery. This is the mini version 1/4 the size of the actual battery to be closer to typical breadboard parts (around 2in wide rathher than 7in). The pads in pcb are sized to accomidate up to 14ga wire (as these batterys will deliver high currents.)
